# Fritzing sketch full-module (saved by Fritzing 0.9.9b)
breadboards: 2

parts:
  J2 = Basic Servo
  M2 = DOIT Esp32 DevKit v1 (30 pins long, 11 pins width) [part_number=ESP32S-PIN30]
  HC-SR04_Sensor_3 = HC-SR04 Ultrasonic Distance Sensor
  Part4 = RFID-RC522-v3
  VCC2 = Battery block 9V
  Part5 = LCD1602-I2C
  VCC3 = Battery block 9V

nets:
  N1: J2.gnd, VCC3.-
  N2: J2.vcc, VCC3.+
  N3: J2.pulse, M2.D12
  GND: M2.GND, HC-SR04_Sensor_3.GND, VCC2.+, Part5.GND
  N4: M2.D2, HC-SR04_Sensor_3.TRIG
  N5: M2.D4, HC-SR04_Sensor_3.ECHO
  N6: M2.D18, Part4.SCK
  N7: M2.D19, Part4.MISO
  N8: M2.D21, Part4.SDA, Part5.SDA
  N9: M2.D22, Part4.RST, Part5.SCL
  N10: M2.D23, Part4.MOSI
  VCC: M2.VIN, HC-SR04_Sensor_3.VCC, VCC2.-, Part5.VCC

notes:
  HC-SR04: Vcc and Gnd must be connected with VIN and GND

custom parts:
  DOIT Esp32 DevKit v1 (30 pins long, 11 pins width): The DOIT Esp32 DevKit v1 is one of the development board created by DOIT to evaluate the ESP-WROOM-32 module. It is based on the ESP32 microcontroller that boasts Wifi, Bluetooth, Ethernet and Low Power support all in a single chip. (vanepp) made breadboard work, adjusted pin numbering and labels and reduced size of schematic and cleaned up pcb. This chip is 30pins long (2 x15) and 11 pins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
  RFID-RC522-v3: A simple China made RFID-RC522 Reader (6x4 cm); do check the pin labels, as this is a MFRC522 based clone.
  LCD1602-I2C: A standard character display, usually with 2x16 characters. Comes in many colors with LCM1602 IIC attached.
